# Fritzing sketch electricLock (saved by Fritzing 0.9.2b)
stripboards: 2

parts:
  Part1 = Arduino Uno (Rev3) - ICSP
  J1 = Basic Servo
  LED1 = LED - 5mm [color="Red (633nm)" package="5 mm [THT]"]
  LED2 = LED - 5mm [color="Green (555nm)" package="5 mm [THT]"]
  U2 = mystery part, 3 pins [chip_label=1329 spacing=300mil]
  U3 = mystery part, 3 pins [chip_label=-]
  S1 = Round Pushbutton
  R1 = Resistor [tolerance=±5% resistance=220 package=THT]
  R2 = Resistor [tolerance=±5% resistance=220 package=THT]
  R3 = Resistor [tolerance=±5% resistance=220 package=THT]
  R4 = Resistor [tolerance=±5% resistance=220 package=THT]
  R5 = Resistor [tolerance=±5% resistance=220 package=THT]

nets:
  N1: Part1.A0, R5.Pin_1
  N2: Part1.D8, S1.leg1, R1.Pin_1
  N3: Part1.D9_PWM, J1.pulse
  N4: Part1.D10_PWM/SS, R2.Pin_1
  N5: Part1.D11_PWM/MOSI, LED1.anode, R3.Pin_0, R3.Pin_1
  GND: Part1.GND, J1.gnd, LED1.cathode, LED2.cathode, U2.pin2, U2.pin3, U3.pin3, R1.Pin_0, R4.Pin_1, R5.Pin_0
  N6: Part1.D7, U3.pin2, R4.Pin_0
  5V: Part1.5V, J1.vcc, U2.pin1, U3.pin1, S1.leg0
  N7: LED2.anode, R2.Pin_0

notes:
  Magnet sensor.
  It detects whether the door is opened or not.
  inclination sensor.
  !!OBSOLATED!!

// code stored in the sketch: electricLock.ino
/**
 * Author: Yamada, Yasuhiro
 * File Name: arduino_servo_switch.ino
 **/

#include <stdio.h>
#include <Servo.h>

const int closeLedPin = 11;
const int openLedPin = 10;

Servo myservo;
const int servoPin = 9;
int pos = 0;

const int magnetPin = 0;
int magnetValue = 0;

const int switchPin = 8;
int nowSwitchState = LOW;
int oldSwitchState = LOW;

const int inclinationPin = 7;
int inclinationState = LOW;

void door_close() {
  myservo.attach( servoPin );
  for ( pos = 35; pos < 145; pos += 1 ) {
    myservo.write( pos );
    //Serial.println(pos);
    delay( 15 );
  }
  myservo.detach();
}

void door_open() {
  myservo.attach( servoPin );
  for ( pos = 145; pos > 35; pos -= 1 ) {
    myservo.write( pos );
    //Serial.println(pos);
    delay( 15 );
  }
  myservo.detach();
}

void setup() {
  Serial.begin(9600);
  pinMode(switchPin, INPUT);
  pinMode(inclinationPin, INPUT);
  pinMode(openLedPin, OUTPUT);
  pinMode(closeLedPin, OUTPUT);
  //initialize the position
  door_close();
}

void loop() {

  char res[128];
  magnetValue = analogRead(magnetPin);
  nowSwitchState = digitalRead(switchPin);
  inclinationState = digitalRead(inclinationPin);

  if (Serial.available()) {
    char tmp = Serial.read();
    int action = tmp - '0';
    switch (action) {
        case 0:
                 door_close();
                 break;
        case 1:
                 door_open();
                 break;
        case 2:
                 /*
                  * response the sensor's data to the PC
                  * Format: [Value of the magnet sensor][Opened or Closed]
                  * 0 > magnetValue > 1023, Opened = 1, Close = 0
                  */
                 sprintf(res, "[%d][%d]", magnetValue, inclinationState == HIGH ? 1 : 0);
                 Serial.println(res);
                 break;
    }
  }

  /* When the switch is pushed */
  if (nowSwitchState == HIGH && oldSwitchState == LOW) {
    door_open();
  }

  /* Door is opened, so the Open Led becomes high. */
  if (inclinationState == HIGH) {
    digitalWrite(openLedPin, HIGH);
    digitalWrite(closeLedPin, LOW);
  }
  /* Door is closed, so the Close Led becomes high. */
  else if (inclinationState == LOW) {
    digitalWrite(openLedPin, LOW);
    digitalWrite(closeLedPin, HIGH);
  }

  oldSwitchState = nowSwitchState;

}
