# Fritzing sketch circuit_diagram (saved by Fritzing 0.9.2b)
stripboards: 1

parts:
  Arduino = Arduino Uno (Rev3) - ICSP
  J1 = Basic Servo
  Magnet_sensor = mystery part, 3 pins [chip_label=1329 spacing=300mil]
  Switch = Round Pushbutton
  R1 = Resistor [tolerance=±5% resistance=220 package=THT]
  R5 = Resistor [tolerance=±5% resistance=220 package=THT]

nets (from the breadboard view):
  N1: Arduino.A0, Magnet_sensor.pin2, R5.Pin_0
  GND: Arduino.GND, J1.gnd, Magnet_sensor.pin3, R1.Pin_0, R5.Pin_1
  N2: Arduino.D8, Switch.leg1, R1.Pin_1
  N3: Arduino.D9_PWM, J1.pulse
  5V: Arduino.5V, J1.vcc, Magnet_sensor.pin1, Switch.leg0

notes:
  Magnet sensor.
  It detects whether the door is opened or not.

// code stored in the sketch: electricLock.ino
/**
 * Author: Yamada, Yasuhiro
 * File Name: arduino_servo_switch.ino
 **/

#include <stdio.h>
#include <Servo.h>

Servo myservo;
const int servoPin = 9;
int pos = 0;

const int magnetPin = 0;
int magnetValue = 0;

const int switchPin = 8;
int nowSwitchState = LOW;
int oldSwitchState = LOW;

void door_close() {
  myservo.attach( servoPin );
  for ( pos = 35; pos < 145; pos += 1 ) {
    myservo.write( pos );
    delay( 15 );
  }
  myservo.detach();
}

void door_open() {
  myservo.attach( servoPin );
  for ( pos = 145; pos > 35; pos -= 1 ) {
    myservo.write( pos );
    delay( 15 );
  }
  myservo.detach();
}

void setup() {
  Serial.begin(9600);
  pinMode(switchPin, INPUT);
  //initialize the position
  door_close();
}

void loop() {

  char res[128];
  magnetValue = analogRead(magnetPin);
  nowSwitchState = digitalRead(switchPin);

  if (Serial.available()) {
    char tmp = Serial.read();
    int action = tmp - '0';
    switch (action) {
        case 0:
                 door_close();
                 break;
        case 1:
                 door_open();
                 break;
        case 2:
                 /*
                  * response the sensor's data to the server
                  * Format: [magnetValue]
                  * 0 > magnetValue > 1023
                  */
                 sprintf(res, "[%d]", magnetValue);
                 Serial.println(res);
                 break;
    }
  }

  /* When the switch is pushed */
  if (nowSwitchState == HIGH && oldSwitchState == LOW) {
    door_open();
  }

  oldSwitchState = nowSwitchState;

}
